# Fritzing sketch schematics (saved by Fritzing 0.9.3b)
breadboards: 1

parts:
  Raspberry_Pi_1 = Raspberry Pi 3 [part_number=RPI-3-V1.2]
  Q1 = npn-Powertransistor [part_number=TIP120 package="TO220 [THT]"]
  D1 = Diode [package=diode-1n4148]
  M1 = DC Motor

nets:
  N1: Raspberry_Pi_1.GIPO20, Q1.base
  N2: Raspberry_Pi_1.GND, Q1.emitter
  N3: Raspberry_Pi_1.5V, D1.C, M1.pin_1
  N4: Q1.collector, D1.A, M1.pin_2

notes:
  Place Touch Screen Display in display port
  TIP120
  DC Motor in Candy Dispenser
  Candy Dispenser
